# Fritzing sketch circuit (saved by Fritzing 0.9.4)
breadboards: 1

parts:
  M1 = E18-D80NK_1 [package=THT]
  Part1 = Arduino Uno (Rev3) - ICSP
  Part2 = LCD1602-I2C
  A1 = MH-FMD buzzer

nets:
  GND: M1.pin1, Part1.GND, Part2.GND, A1.Pin_3
  5V: M1.pin2, Part1.5V, Part2.VCC, A1.Pin_1
  N1: M1.pin3, Part1.D2
  N2: Part1.A4/SDA, Part2.SDA
  N3: Part1.A5/SCL, Part2.SCL
  N4: Part1.D3_PWM, A1.Pin_2

custom parts:
  E18-D80NK_1: E18-D80NK Proximity Sensor module.
  LCD1602-I2C: A standard character display, usually with 2x16 characters. Comes in many colors with LCM1602 IIC attached.
  MH-FMD buzzer: MH-FMD buzzer.
